# Fritzing sketch shooCat (saved by Fritzing 0.8.7b)
circuit board: 3.3204cm x 6.36019cm
breadboards: 1

parts:
  C1 = Ceramic Capacitor [capacitance=0.1µF package="100 mil [THT, multilayer]"]
  D1 = Rectifier Diode [part_number=1N4001 package="300 mil [THT]"]
  R1 = Resistor [tolerance=±5% resistance=1k package=THT]
  PIR2 = PIR sensor
  PIR1 = PIR sensor
  Speaker = Piezo Speaker
  R2 = Resistor [tolerance=±5% resistance=220 package=THT]
  Arduino_Micro_rev3 = Arduino Micro (Rev3)
  vibrate = DC Motor
  R3 = Resistor [tolerance=±5% resistance=120 package=THT]
  LED = LED - 5mm [color="Red (633nm)" package="5 mm [THT]"]
  volume = POT [package=3362u]
  NPN = NPN-Transistor [package="TO92 [THT]"]
  on/off = Square Pushbutton
  power = Screw terminal - 2 pins [package=THT]

nets:
  N1: C1.0, D1.anode, vibrate.pin_2, NPN.C
  VDD: C1.1, D1.cathode, PIR2.VDD, PIR1.VDD, Arduino_Micro_rev3.5V, vibrate.pin_1
  N2: R1.Pin_0, Arduino_Micro_rev3.D6_PWM/A7
  N3: R1.Pin_1, NPN.B
  N4: PIR2.SIG, Arduino_Micro_rev3.D7
  GND: PIR2.GND, PIR1.GND, Arduino_Micro_rev3.GND, LED.anode, volume.S, NPN.E, power.pin2
  N5: PIR1.SIG, Arduino_Micro_rev3.D2/SDA
  N6: Speaker.pin1, R3.Pin_0
  N7: Speaker.pin2, Arduino_Micro_rev3.D5_PWM
  N8: R2.Pin_0, Arduino_Micro_rev3.D12_PWM/A11
  N9: R2.Pin_1, LED.cathode
  N10: Arduino_Micro_rev3.VIN, on/off.leg0
  N11: R3.Pin_1, volume.E
  N12: on/off.leg1, power.pin1

notes:
  shoo cat
  RKH 2014
  -  +
